# Fritzing sketch SmartPlant (saved by Fritzing 0.9.9b)
breadboards: 1

parts:
  Argon1 = Particle Argon
  Q1 = PNP-Transistor [package="TO92 [THT]"]
  R1 = Resistor [tolerance=±5% resistance=2.2k package="2512 [SMD]"]
  R2 = Resistor [tolerance=±5% resistance=220 package="2512 [SMD]"]
  Relay1 = Relay - 6 pins [package="DIP (Dual Inline) [THT]"]
  SENS1 = SoilWatch 10
  M1 = DC Motor
  OLED_I2C1 = OLED 128x64 I2C Monochrome Display
  M2 = BMP280
  Part1 = MQ-131 breakout
  Grove1 = Grove Dust Sensor

nets:
  VCC: Argon1.3.3V, Relay1.VCC, SENS1.VCC, OLED_I2C1.VDD, M2.VIN, Part1.VCC, Grove1.VCC
  GND: Argon1.GND, Q1.E, R2.Pin_0, Relay1.GND, SENS1.GND, M1.pin_1, OLED_I2C1.GND, M2.GND, Part1.GND, Grove1.GND
  N1: Argon1.A0, SENS1.OUT
  N2: Argon1.A1, Grove1.SIG
  N3: Argon1.A2, Part1.AO
  N4: Argon1.MI, Q1.B, R2.Pin_1
  N5: Argon1.SDA, OLED_I2C1.SDA, M2.SDA
  N6: Argon1.SCL, OLED_I2C1.SCK, M2.SCL
  N7: Argon1.VUSB, R1.Pin_1, Relay1.COM
  N8: Q1.C, R1.Pin_0, Relay1.IN
  N9: Relay1.ON, M1.pin_2

custom parts:
  Particle Argon: The Argon is a powerful Wi-Fi enabled development board that can act as either a standalone Wi-Fi endpoint or Wi-Fi enabled gateway for Particle Mesh networks. It is based on the Nordic nRF52840 and has built-in battery charging circuitry so it’s easy to connect a Li-Po and deploy your local network in minutes. The Argon is great for connecting existing projects to the Particle Device Cloud or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
  Relay - 6 pins: A DIP stand-in part for whatever IC you want. With 6 pins on a 900mil dual inline package (DIP) footprint.
  SoilWatch 10: SoilWatch 10 - Capacitive soil moisture sensor
  BMP280: Temperature Humidity Barometric presure Sensor, I2C
  MQ-131 breakout: SKU: 101282
  Grove Dust Sensor: PPD42 Grove Dust Sensor
